// Logisim project ics-quiz-document.circ as structural Verilog: 2 circuits, main circuit main
module main (
  input  W,
  input  X,
  input  Y,
  input  Z,
  output out_5
);

  wire and_1_out, and_2_out, and_3_out, and_4_out, and_5_out, not_1_out, not_2_out, not_3_out, not_4_out,
       not_5_out;

  and and_1 (and_1_out, W, X);
  and and_2 (and_2_out, W, X, Y);
  or or_1 (out_5, and_1_out, and_5_out, and_2_out, and_4_out, and_3_out);
  not not_1 (not_1_out, W);
  and and_3 (and_3_out, not_1_out, Y, Z);
  not not_2 (not_2_out, Y);
  not not_3 (not_3_out, W);
  and and_4 (and_4_out, not_3_out, not_2_out, Z);
  not not_4 (not_4_out, W);
  and and_5 (and_5_out, not_4_out, X, Y, not_5_out);
  not not_5 (not_5_out, Z);
endmodule

module lod (
  input  Z,
  input  Y,
  input  X,
  input  W,
  output out_5
);

  wire and_1_out, not_1_out, or_1_out, or_2_out;

  and and_1 (and_1_out, Y, X);
  not not_1 (not_1_out, W);
  or or_1 (or_1_out, X, not_1_out);
  or or_2 (or_2_out, Z, and_1_out);
  and and_2 (out_5, or_2_out, or_1_out);
endmodule
