// Logisim project ics-quiz-lab2.circ as structural Verilog: 9 circuits, main circuit OR
module OR (
  input  A,
  input  B,
  output Y
);

  or or_1 (Y, A, B);
endmodule

module AND (
  input  A,
  input  B,
  output Y
);

  and and_1 (Y, A, B);
endmodule

module Interter (
  input  A,
  output Y
);

  not not_1 (Y, A);
endmodule

module NOR (
  input  A,
  input  B,
  output Y
);

  wire or_1_out;

  or or_1 (or_1_out, A, B);
  not not_1 (Y, or_1_out);
endmodule

module NAND (
  input  A,
  input  B,
  output Y
);

  wire and_1_out;

  and and_1 (and_1_out, A, B);
  not not_1 (Y, and_1_out);
endmodule

module OR2 (
  input  A,
  input  B,
  input  C,
  output Y
);

  wire or_1_out;

  or or_1 (or_1_out, A, B);
  or or_2 (Y, or_1_out, C);
endmodule

module AND2 (
  input  A,
  input  B,
  input  C,
  output Y
);

  wire and_1_out;

  and and_1 (and_1_out, A, B);
  and and_2 (Y, and_1_out, C);
endmodule

module NAND2 (
  input  A,
  input  B,
  input  C,
  output Y
);

  wire and_1_out, and_2_out, not_1_out;

  and and_1 (and_1_out, A, B);
  not not_1 (not_1_out, and_1_out);
  and and_2 (and_2_out, not_1_out, C);
  not not_2 (Y, and_2_out);
endmodule

module NOR2 (
  input  A,
  input  B,
  input  C,
  output Y
);

  wire not_1_out, or_1_out, or_2_out;

  or or_1 (or_1_out, A, B);
  not not_1 (not_1_out, or_1_out);
  not not_2 (Y, or_2_out);
  or or_2 (or_2_out, not_1_out, C);
endmodule
