// Logisim project ics-quiz-lab3.circ as structural Verilog: 2 circuits, main circuit main
module main (
  input  W,
  input  X,
  input  Y,
  input  Z,
  output F
);

  wire and_1_out, and_2_out, and_3_out, and_4_out, and_5_out, not_1_out, not_2_out, not_3_out, not_4_out,
       not_5_out;

  not not_1 (not_1_out, W);
  not not_2 (not_2_out, W);
  not not_3 (not_3_out, Y);
  not not_4 (not_4_out, W);
  not not_5 (not_5_out, Z);
  and and_1 (and_1_out, W, X);
  and and_2 (and_2_out, W, X, Y);
  and and_3 (and_3_out, not_1_out, Y, Z);
  and and_4 (and_4_out, not_2_out, not_3_out, Z);
  and and_5 (and_5_out, not_4_out, X, Y, not_5_out);
  or or_1 (F, and_1_out, and_2_out, and_3_out, and_4_out, and_5_out);
endmodule

module lodmain (
  input  W,
  input  X,
  input  Y,
  input  Z
);
endmodule
