// Logisim project ics-quiz-seg.circ as structural Verilog: 2 circuits, main circuit main
module main (
  input  A,
  input  B,
  input  C,
  input  D
);

  wire under_1_c0, under_1_c1, under_1_c2, under_1_c3, under_1_c4, under_1_c5, under_1_c6;

  under under_1 (
    .A(A), .B(B), .C(C), .D(D), .C0(under_1_c0), .C1(under_1_c1), .C2(under_1_c2), .C3(under_1_c3),
    .C4(under_1_c4), .C5(under_1_c5), .C6(under_1_c6));
  _7_Segment_Display u_7_segment_display_1 (
    .g(under_1_c6), .f(under_1_c5), .a(under_1_c0), .b(under_1_c1), .e(under_1_c4), .d(under_1_c3),
    .c(under_1_c2));  // open: dp
endmodule

module under (
  input  A,
  input  B,
  input  C,
  input  D,
  output C0,
  output C1,
  output C2,
  output C3,
  output C4,
  output C5,
  output C6
);

  wire B_nC_out, B_nCD_out, B_nD_out, BD_out, C_nD_out, CD_out, nB_nD_out, nBC_out, nC_nD_out, not_1_out,
       not_2_out, not_3_out;

  not not_1 (not_1_out, B);
  not not_2 (not_2_out, C);
  not not_3 (not_3_out, D);
  and BD (BD_out, B, D);
  and nB_nD (nB_nD_out, not_1_out, not_3_out);
  and CD (CD_out, C, D);
  and nC_nD (nC_nD_out, not_2_out, not_3_out);
  and C_nD (C_nD_out, C, not_3_out);
  and nBC (nBC_out, not_1_out, C);
  and B_nCD (B_nCD_out, B, not_2_out, D);
  and B_nC (B_nC_out, B, not_2_out);
  and B_nD (B_nD_out, B, not_3_out);
  or u_C0 (C0, BD_out, nB_nD_out, A, C);
  or u_C1 (C1, not_1_out, CD_out, nC_nD_out);
  or u_C2 (C2, B, not_2_out, D);
  or u_C3 (C3, nB_nD_out, C_nD_out, nBC_out, B_nCD_out);
  or u_C4 (C4, C_nD_out, nB_nD_out);
  or u_C5 (C5, A, B_nC_out, B_nD_out, nC_nD_out);
  or u_C6 (C6, A, B_nC_out, B_nD_out, nBC_out);
endmodule
