// Logisim project ics-quiz-xor-project.circ as structural Verilog: 4 circuits, main circuit main
module main (
  input  A3,
  input  A2,
  input  A1,
  input  A0,
  input  B3,
  input  B2,
  input  B1,
  input  B0,
  output W
);

  _4b_cmp u_4b_cmp_1 (.A3(A3), .A2(A2), .A1(A1), .A0(A0), .B3(B3), .B2(B2), .B1(B1), .B0(B0), .W(W));
endmodule

module myXOR (
  input  A,
  input  B,
  output z
);

  wire and_1_out, and_2_out, not_1_out, not_2_out;

  not not_1 (not_1_out, A);
  not not_2 (not_2_out, B);
  and and_1 (and_1_out, A, not_2_out);
  and and_2 (and_2_out, not_1_out, B);
  or or_1 (z, and_1_out, and_2_out);
endmodule

module myXNOR (
  input  A,
  input  B,
  output Z
);

  wire and_1_out, and_2_out, not_1_out, not_2_out;

  not not_1 (not_1_out, A);
  not not_2 (not_2_out, B);
  and and_1 (and_1_out, not_1_out, not_2_out);
  and and_2 (and_2_out, A, B);
  or or_1 (Z, and_1_out, and_2_out);
endmodule

module _4b_cmp (
  input  A3,
  input  A2,
  input  A1,
  input  A0,
  input  B3,
  input  B2,
  input  B1,
  input  B0,
  output W
);

  wire and_1_out, and_2_out, myxnor_1_z, myxnor_2_z, myxnor_3_z, myxnor_4_z;

  myXNOR myxnor_1 (.A(A3), .B(B3), .Z(myxnor_1_z));
  myXNOR myxnor_2 (.A(A2), .B(B2), .Z(myxnor_2_z));
  myXNOR myxnor_3 (.A(A1), .B(B1), .Z(myxnor_3_z));
  myXNOR myxnor_4 (.A(A0), .B(B0), .Z(myxnor_4_z));
  and and_1 (and_1_out, myxnor_1_z, myxnor_2_z);
  and and_2 (and_2_out, myxnor_3_z, myxnor_4_z);
  and and_3 (W, and_1_out, and_2_out);
endmodule
