// Logisim project ics-lab-01-completed.circ as structural Verilog: 5 circuits, main circuit main
module main (
  input  in_1,
  input  in_2,
  input  in_3,
  input  in_4,
  input  in_5,
  input  in_6,
  input  in_7,
  input  in_8,
  output W
);

  Four_Bit_Comparator four_bit_comparator_1 (
    .A3(in_1), .A2(in_2), .A1(in_3), .A0(in_4), .B3(in_5), .B2(in_6), .B1(in_7), .B0(in_8), .W(W));
endmodule

module myXOR (
  input  A,
  input  B,
  output Z
);

  wire and_1_out, and_2_out, not_1_out, not_2_out;

  not not_1 (not_1_out, A);
  not not_2 (not_2_out, B);
  and and_1 (and_1_out, A, not_2_out);
  and and_2 (and_2_out, not_1_out, B);
  or or_1 (Z, and_1_out, and_2_out);
endmodule

module myXNOR (
  input  A,
  input  B,
  output Z
);

  wire and_1_out, and_2_out, not_1_out, not_2_out, or_1_out;

  not not_1 (not_1_out, A);
  not not_2 (not_2_out, B);
  and and_1 (and_1_out, A, not_2_out);
  and and_2 (and_2_out, not_1_out, B);
  or or_1 (or_1_out, and_1_out, and_2_out);
  not not_3 (Z, or_1_out);
endmodule

module Schematic_Diagram (
  input  B5,
  input  B4,
  input  B3,
  input  B2,
  input  B1,
  input  B0
);

  wire myxor_1_z, myxor_2_z, myxor_3_z, myxor_4_z, myxor_5_z;

  myXOR myxor_1 (.A(B5), .B(B4), .Z(myxor_1_z));
  myXOR myxor_2 (.A(B3), .B(B2), .Z(myxor_2_z));
  myXOR myxor_3 (.A(B1), .B(B0), .Z(myxor_3_z));
  myXOR myxor_4 (.A(myxor_1_z), .B(myxor_2_z), .Z(myxor_4_z));
  myXOR myxor_5 (.A(myxor_4_z), .B(myxor_3_z), .Z(myxor_5_z));
  LED W (.in(myxor_5_z));
endmodule

module Four_Bit_Comparator (
  input  A3,
  input  A2,
  input  A1,
  input  A0,
  input  B3,
  input  B2,
  input  B1,
  input  B0,
  output W
);

  wire and_1_out, and_2_out, myxnor_1_z, myxnor_2_z, myxnor_3_z, myxnor_4_z;

  myXNOR myxnor_1 (.A(A3), .B(B3), .Z(myxnor_1_z));
  myXNOR myxnor_2 (.A(A2), .B(B2), .Z(myxnor_2_z));
  myXNOR myxnor_3 (.A(A1), .B(B1), .Z(myxnor_3_z));
  myXNOR myxnor_4 (.A(A0), .B(B0), .Z(myxnor_4_z));
  and and_1 (and_1_out, myxnor_1_z, myxnor_2_z);
  and and_2 (and_2_out, myxnor_3_z, myxnor_4_z);
  and and_3 (W, and_1_out, and_2_out);
endmodule
