// Logisim project quiz-2-test.circ as structural Verilog: 3 circuits, main circuit main
module main (
  input  a,
  input  b,
  input  c,
  input  d
);

  wire graderv2_1_x, graderv2_1_y, graderv2_1_z;
  wire [6:0] chardecoderv2_1_out_4;

  graderV2 graderv2_1 (.A(a), .B(b), .C(c), .D(d), .x(graderv2_1_x), .y(graderv2_1_y), .z(graderv2_1_z));
  charDecoderV2 chardecoderv2_1 (.x(graderv2_1_x), .y(graderv2_1_y), .z(graderv2_1_z), .out_4(chardecoderv2_1_out_4));
  _7_Segment_Display #(.decimalPoint("false")) u_7_segment_display_1 (
    .g(chardecoderv2_1_out_4[6]), .f(chardecoderv2_1_out_4[5]), .a(chardecoderv2_1_out_4[0]),
    .b(chardecoderv2_1_out_4[1]), .e(chardecoderv2_1_out_4[4]), .d(chardecoderv2_1_out_4[3]),
    .c(chardecoderv2_1_out_4[2]));
endmodule

module charDecoderV2 (
  input  x,
  input  y,
  input  z,
  output [6:0] out_4
);

  wire not_2_out, not_3_out;

  not not_1 (out_4[3], x);
  not not_2 (not_2_out, y);
  not not_3 (not_3_out, z);
  or c0 (out_4[0], x, not_3_out);
  and c1 (out_4[1], z, not_2_out);
  or c5 (out_4[5], y, x);
  or c6 (out_4[6], x, z);

  assign {out_4[4], out_4[2]} = {1'b1, z};
endmodule

module graderV2 (
  input  A,
  input  B,
  input  C,
  input  D,
  output x,
  output y,
  output z
);

  wire and_1_out, and_2_out, and_3_out, and_4_out, and_5_out, and_6_out, not_1_out, not_2_out, not_3_out,
       not_4_out;

  not not_1 (not_1_out, A);
  not not_2 (not_2_out, B);
  not not_3 (not_3_out, C);
  not not_4 (not_4_out, D);
  and and_1 (and_1_out, not_2_out, not_1_out);
  and and_2 (and_2_out, A, not_2_out);
  and and_3 (and_3_out, C, B, A);
  and and_4 (and_4_out, A, not_3_out, not_4_out);
  and and_5 (and_5_out, D, B, A);
  and and_6 (and_6_out, A, C, D);
  or or_1 (x, and_5_out, and_3_out, and_1_out);
  or or_2 (y, and_4_out, and_2_out);
  or or_3 (z, and_6_out, B);
endmodule
